// Logisim project s-mips.circ as structural Verilog
module S_MIPS_Board (
  input  DESHABILITAR_DISPATCHER,
  output halt
);

  wire button_1_out, CLK, CS, d_ff_1_q, LCLR, LoadRAM, LoadRAMOn, LW, R_R_W, R_W, ram_dispatcher_1_finished,
       RCS, Reset_out, RST, TTY_EN;
  wire [2:0] KDB;
  wire [3:0] LMask, Mask, ram_1_read_time, ram_1_write_time, RMask;
  wire [6:0] KDB_DATA, TTY_DATA;
  wire [15:0] Addr, LAddr, RAddr;
  wire [31:0] I0, I1, I2, I3, LData, ram_1_data_out_0, ram_1_data_out_1, ram_1_data_out_2, ram_1_data_out_3,
       RI0, RI1, RI2, RI3;

  TTY #(.rows(25), .cols(80)) tty_1 (.data(TTY_DATA), .clk(CLK), .we(TTY_EN), .clr(RST));
  not not_1 (LoadRAMOn, ram_dispatcher_1_finished);
  RAM_Dispatcher ram_dispatcher_1 (
    .WriteTime(ram_1_write_time), .Clock(CLK), .Data(LData), .Address(LAddr), .Mask(LMask),
    .Finished(ram_dispatcher_1_finished), .Write(LW), .CLR(LCLR));
  Keyboard #(.buflen(64)) keyboard_1 (.clk(CLK), .re(KDB[0]), .avail(KDB[2]), .data(KDB_DATA));  // open: clr
  RAM ram_1 (
    .Address(RAddr), .Data_Out_0(ram_1_data_out_0), .Data_Out_1(ram_1_data_out_1),
    .Data_Out_2(ram_1_data_out_2), .Data_Out_3(ram_1_data_out_3), .Data_In_0(RI0), .Data_In_1(RI1),
    .Data_In_2(RI2), .Data_In_3(RI3), .Mask(RMask), .nRead_Write(R_R_W), .Chip_Select(RCS),
    .Read_Time(ram_1_read_time), .Reset(button_1_out), .Write_Time(ram_1_write_time));
  Button button_1 (.out(button_1_out));
  D_Flip_Flop d_ff_1 (.clk(CLK), .D(1'b1), .Q(d_ff_1_q), .reset(Reset_out));  // open: Qn, preset, en
  Button Reset (.out(Reset_out));
  S_MIPS s_mips_1 (
    .Kbd_Enable(KDB[0]), .Address(Addr), .Kbd_Clear(KDB[1]), .Kbd_Available(KDB[2]), .RAM_In_0(I0),
    .Kbd_ASCII_Data(KDB_DATA), .RAM_In_1(I1), .TTY_Enable(TTY_EN), .RAM_In_2(I2), .RAM_In_3(I3),
    .TTY_ASCII_Data(TTY_DATA), .Reset(RST), .RAM_Out_0(ram_1_data_out_0), .Clock(CLK),
    .RAM_Out_1(ram_1_data_out_1), .Stop(halt), .RAM_Out_2(ram_1_data_out_2), .RAM_Out_3(ram_1_data_out_3),
    .Mask(Mask), .Read_Time(ram_1_read_time), .Write_Time(ram_1_write_time), .nRead_Write(R_W),
    .Chip_Select(CS));
  D_Flip_Flop d_ff_2 (.clk(CLK), .D(d_ff_1_q), .Qn(LCLR), .reset(Reset_out));  // open: Q, preset, en
  or or_1 (RST, LCLR, LoadRAM);
  Clock clock_1 (.out(CLK));
  Multiplexer #(.width(32), .enable("false")) multiplexer_1 (.in0(I0), .in1(LData), .out(RI0), .sel(LoadRAM));
  Multiplexer #(.width(32), .enable("false")) multiplexer_2 (.in0(I1), .in1(LData), .out(RI1), .sel(LoadRAM));
  Multiplexer #(.width(32), .enable("false")) multiplexer_3 (.in0(I2), .in1(LData), .out(RI2), .sel(LoadRAM));
  Multiplexer #(.width(32), .enable("false")) multiplexer_4 (.in0(I3), .in1(LData), .out(RI3), .sel(LoadRAM));
  and and_1 (LoadRAM, ~DESHABILITAR_DISPATCHER, LoadRAMOn);  // AND_Gate
  Multiplexer #(.width(16), .enable("false")) multiplexer_5 (.in0(Addr), .in1(LAddr), .out(RAddr), .sel(LoadRAM));
  Multiplexer #(.width(4), .enable("false")) multiplexer_6 (.in0(Mask), .in1(LMask), .out(RMask), .sel(LoadRAM));
  Multiplexer #(.enable("false")) multiplexer_7 (.in0(CS), .in1(LW), .out(RCS), .sel(LoadRAM));
  Multiplexer #(.enable("false")) multiplexer_8 (.in0(R_W), .in1(LW), .out(R_R_W), .sel(LoadRAM));

  // Notes on the sheet:
  //   NO MODIFICAR
  //   Keyboard
endmodule

module RAM (
  input  [15:0] Address,
  input  [31:0] Data_In_0,
  input  [31:0] Data_In_1,
  input  [31:0] Data_In_2,
  input  [31:0] Data_In_3,
  input  [3:0] Mask,
  input  nRead_Write,
  input  Chip_Select,
  input  Reset,
  output [31:0] Data_Out_0,
  output [31:0] Data_Out_1,
  output [31:0] Data_Out_2,
  output [31:0] Data_Out_3,
  output [3:0] Read_Time,
  output [3:0] Write_Time
);

  wire and_2_out, and_3_out, and_4_out, and_5_out, and_6_out, and_7_out, and_8_out, and_9_out, Changed, CLK,
       comparator_2_eq, comparator_3_eq, comparator_4_eq, comparator_5_eq, comparator_6_eq, Count,
       demultiplexer_3_out0, Idle, Idle_q, Load, Load0, Load1, nand_1_out, or_1_out, or_2_out, or_3_out,
       or_4_out, or_5_out, or_6_out, or_7_out, or_8_out, or_9_out, or_10_out, Proc_q, Update_Mem, Zero_Time;
  wire [3:0] counter_1_q, multiplexer_1_out, subtractor_1_out;
  wire [31:0] register_1_q, register_2_q, register_3_q, register_4_q, register_5_q;

  // Probe on 4'b0011
  // Probe on 4'b0010
  Multiplexer #(.width(4), .enable("false")) multiplexer_1 (
    .in0(4'b0011), .in1(4'b0010), .out(multiplexer_1_out), .sel(nRead_Write));
  or or_1 (or_1_out, Idle, Update_Mem);
  or or_2 (or_2_out, ~Chip_Select, Reset);  // OR_Gate
  Subtractor #(.width(4)) subtractor_1 (.a(multiplexer_1_out), .b(4'b0010), .out(subtractor_1_out));  // open: bin, bout
  Demultiplexer #(.enable("false")) demultiplexer_1 (.out0(Idle), .out1(Load0), .in(Idle_q), .sel(Changed));
  D_Flip_Flop u_Idle (.clk(CLK), .D(or_1_out), .Q(Idle_q), .preset(or_2_out));  // open: Qn, en, reset
  // Probe on counter_1_q
  Counter #(.width(4), .max('hf)) counter_1 (
    .load(Load), .D(subtractor_1_out), .count(Count), .Q(counter_1_q), .clk(CLK), .clr(or_3_out));  // open: carry
  or or_3 (or_3_out, ~Chip_Select, Reset);  // OR_Gate
  Comparator #(.width(4), .mode("unsigned")) comparator_1 (
    .a(4'b0000), .b(counter_1_q), .eq(Zero_Time));  // open: gt, lt
  or or_4 (or_4_out, Count, Load0, Load1);
  Register #(.width(32)) register_1 (.D(Data_In_0), .en(Chip_Select), .Q(register_1_q), .clk(CLK), .clr(or_5_out));
  or or_5 (or_5_out, ~Chip_Select, Reset);  // OR_Gate
  Register #(.width(32)) register_2 (.D(Data_In_1), .en(Chip_Select), .Q(register_2_q), .clk(CLK), .clr(or_6_out));
  or or_6 (or_6_out, ~Chip_Select, Reset);  // OR_Gate
  Register #(.width(32)) register_3 (.D(Data_In_2), .en(Chip_Select), .Q(register_3_q), .clk(CLK), .clr(or_7_out));
  or or_7 (or_7_out, ~Chip_Select, Reset);  // OR_Gate
  Register #(.width(32)) register_4 (.D(Data_In_3), .en(Chip_Select), .Q(register_4_q), .clk(CLK), .clr(or_8_out));
  or or_8 (or_8_out, ~Chip_Select, Reset);  // OR_Gate
  Register #(.width(32)) register_5 (
    .D({{11{1'b1}}, nRead_Write, Mask, Address}), .en(Chip_Select), .Q(register_5_q), .clk(CLK),
    .clr(or_9_out));
  or or_9 (or_9_out, ~Chip_Select, Reset);  // OR_Gate
  D_Flip_Flop Proc (.clk(CLK), .D(or_4_out), .Q(Proc_q), .reset(or_10_out));  // open: Qn, preset, en
  or or_10 (or_10_out, ~Chip_Select, Reset);  // OR_Gate
  Demultiplexer #(.enable("false")) demultiplexer_2 (
    .out0(Count), .out1(Update_Mem), .in(demultiplexer_3_out0), .sel(Zero_Time));
  Demultiplexer #(.enable("false")) demultiplexer_3 (
    .out0(demultiplexer_3_out0), .out1(Load1), .in(Proc_q), .sel(Changed));
  Clock clock_1 (.out(CLK));
  Comparator #(.width(32)) comparator_2 (.a(register_1_q), .b(Data_In_0), .eq(comparator_2_eq));  // open: gt, lt
  Comparator #(.width(32)) comparator_3 (.a(register_2_q), .b(Data_In_1), .eq(comparator_3_eq));  // open: gt, lt
  Comparator #(.width(32)) comparator_4 (.a(register_3_q), .b(Data_In_2), .eq(comparator_4_eq));  // open: gt, lt
  Comparator #(.width(32)) comparator_5 (.a(register_4_q), .b(Data_In_3), .eq(comparator_5_eq));  // open: gt, lt
  Comparator #(.width(32)) comparator_6 (
    .a(register_5_q), .b({{11{1'b1}}, nRead_Write, Mask, Address}), .eq(comparator_6_eq));  // open: gt, lt
  nand nand_1 (nand_1_out, comparator_6_eq, comparator_2_eq, comparator_3_eq, comparator_4_eq, comparator_5_eq);
  and and_1 (Changed, nand_1_out, Chip_Select);
  or or_11 (Load, Count, Load1, Load0);
  and and_2 (and_2_out, Mask[0], Update_Mem, nRead_Write);
  and and_3 (and_3_out, Mask[1], Update_Mem, nRead_Write);
  and and_4 (and_4_out, Mask[2], Update_Mem, nRead_Write);
  and and_5 (and_5_out, Mask[3], Update_Mem, nRead_Write);
  RAM_part #(.addrWidth(16), .dataWidth(32), .bus("separate")) ram_1 (
    .addr(Address), .din(Data_In_0), .data(Data_Out_0), .str(and_2_out), .sel(Chip_Select), .clk(CLK),
    .ld(and_6_out), .clr(Reset));
  and and_6 (and_6_out, ~nRead_Write, Idle);  // AND_Gate
  RAM_part #(.addrWidth(16), .dataWidth(32), .bus("separate")) ram_2 (
    .addr(Address), .din(Data_In_1), .data(Data_Out_1), .str(and_3_out), .sel(Chip_Select), .clk(CLK),
    .ld(and_7_out), .clr(Reset));
  and and_7 (and_7_out, ~nRead_Write, Idle);  // AND_Gate
  RAM_part #(.addrWidth(16), .dataWidth(32), .bus("separate")) ram_3 (
    .addr(Address), .din(Data_In_2), .data(Data_Out_2), .str(and_4_out), .sel(Chip_Select), .clk(CLK),
    .ld(and_8_out), .clr(Reset));
  and and_8 (and_8_out, ~nRead_Write, Idle);  // AND_Gate
  RAM_part #(.addrWidth(16), .dataWidth(32), .bus("separate")) ram_4 (
    .addr(Address), .din(Data_In_3), .data(Data_Out_3), .str(and_5_out), .sel(Chip_Select), .clk(CLK),
    .ld(and_9_out), .clr(Reset));
  and and_9 (and_9_out, ~nRead_Write, Idle);  // AND_Gate

  assign Read_Time = 4'b0011;
  assign Write_Time = 4'b0010;

  // Other names for the same wires on the sheet: M0 = Mask[0]; M1 = Mask[1]; M2 = Mask[2]; M3 = Mask[3];
  //   RW = nRead_Write; CLR = Reset; CS = Chip_Select; Load2 = Count

  // Notes on the sheet:
  //   NO MODIFICAR
  //   excepto quizás los valores RT y WT
  //   BANK0
  //   BANK1
  //   BANK2
  //   BANK3
endmodule

module RAM_Dispatcher (
  input  [3:0] WriteTime,
  input  Clock,
  input  CLR,
  output [31:0] Data,
  output [15:0] Address,
  output [3:0] Mask,
  output Finished,
  output Write
);

  wire demultiplexer_2_out1, demultiplexer_3_out1, End, IDLE_q, IncAddr, Load, or_1_out, or_2_out, While_q,
       WriteEnd;
  wire [3:0] counter_1_q;
  wire [31:0] CurrentAddress_q;

  Counter #(.width(32), .max('hffffffff)) CurrentAddress (
    .count(IncAddr), .Q({CurrentAddress_q[31:18], Address, CurrentAddress_q[1:0]}), .clk(Clock), .clr(CLR));  // open: load, D, carry
  or or_1 (or_1_out, IncAddr, demultiplexer_3_out1, Finished);
  D_Flip_Flop IDLE (.clk(Clock), .D(or_1_out), .Q(IDLE_q), .preset(CLR));  // open: Qn, en, reset
  Demultiplexer #(.enable("false")) demultiplexer_1 (.out0(Load), .out1(Finished), .in(IDLE_q), .sel(End));
  D_Flip_Flop While (.clk(Clock), .D(or_2_out), .Q(While_q), .reset(CLR));  // open: Qn, preset, en
  or or_2 (or_2_out, Write, Load);
  RAM_part #(.addrWidth(18), .dataWidth(32)) ram_1 (
    .addr({Address, CurrentAddress_q[1:0]}), .data(Data), .clk(Clock));  // open: sel, ld, clr
  Demultiplexer #(.enable("false")) demultiplexer_2 (
    .out0(Write), .out1(demultiplexer_2_out1), .in(While_q), .sel(WriteEnd));
  Decoder #(.select(2)) decoder_1 (
    .out0(Mask[0]), .out1(Mask[1]), .out2(Mask[2]), .out3(Mask[3]), .sel(CurrentAddress_q[1:0]));  // open: en
  Demultiplexer #(.enable("false")) demultiplexer_3 (
    .out0(IncAddr), .out1(demultiplexer_3_out1), .in(demultiplexer_2_out1), .sel(End));
  Counter #(.width(4), .max('hf)) counter_1 (
    .load(Load), .D(WriteTime), .count(Write), .Q(counter_1_q), .clk(Clock));  // open: carry, clr
  Comparator #(.width(32)) comparator_1 (.a(Data), .b({32{1'b1}}), .eq(End));  // open: gt, lt
  Comparator #(.width(4)) comparator_2 (.a(4'b0000), .b(counter_1_q), .eq(WriteEnd));  // open: gt, lt

  // Other names for the same wires on the sheet: CLK = Clock; Count = Write; WT[3:0] = WriteTime
endmodule

module S_MIPS (
  input  [31:0] RAM_Out_0,
  input  Kbd_Available,
  input  [3:0] Read_Time,
  input  [3:0] Write_Time,
  input  [6:0] Kbd_ASCII_Data,
  input  [31:0] RAM_Out_1,
  input  [31:0] RAM_Out_2,
  input  Reset,
  input  [31:0] RAM_Out_3,
  input  Clock,
  output Kbd_Enable,
  output [3:0] Mask,
  output Kbd_Clear,
  output [31:0] RAM_In_0,
  output [31:0] RAM_In_1,
  output TTY_Enable,
  output nRead_Write,
  output Chip_Select,
  output [6:0] TTY_ASCII_Data,
  output [31:0] RAM_In_2,
  output [31:0] RAM_In_3,
  output [15:0] Address,
  output Stop
);

  wire cache_data_1_cs, cache_instruction_1_cs, CDE, CIE, control_unit_1_load_pc, control_unit_1_mul_or_div,
       control_unit_1_register_address_selector, control_unit_1_rf_write, control_unit_1_sp_selector_input,
       D_I, data_path_1_negative, data_path_1_zero, Finish_CD, Finish_IC, instruction_decoder_1_is_jump,
       instruction_decoder_1_is_kbd, instruction_decoder_1_is_push, instruction_decoder_1_is_push_2,
       instruction_decoder_1_is_rnd, instruction_decoder_1_is_sw, instruction_decoder_1_li_selector,
       instruction_decoder_1_pop_or_push, put_zeros, R_W_CD, R_W_CI;
  wire [1:0] instruction_decoder_1_b_selector, instruction_decoder_1_register_input_selector,
       instruction_decoder_1_special_selector;
  wire [2:0] instruction_decoder_1_bc_path, instruction_decoder_1_cu_path;
  wire [3:0] instruction_decoder_1_alu_op;
  wire [4:0] instruction_decoder_1_out_5, instruction_decoder_1_out_6, instruction_decoder_1_out_7;
  wire [15:0] cache_data_1_last_ra, cache_data_1_out_13, cache_instruction_1_out_13, instruction_decoder_1_se;
  wire [25:0] instruction_decoder_1_destiny;
  wire [31:0] branch_control_1_out_9, cache_instruction_1_out_14, Data, data_path_1_address_to_cd,
       data_path_1_data_to_cd, data_path_1_jump_register, PC, sign_extender_1_immediate;

  Cache_Instruction cache_instruction_1 (
    .Last_Ram_Address(cache_data_1_last_ra), .CLK(Clock), .in_2(CIE), .RW(R_W_CI), .in_4(Read_Time),
    .Reset(Reset), .out_14(cache_instruction_1_out_14), .out_13(cache_instruction_1_out_13),
    .out_12(Finish_IC), .CS(cache_instruction_1_cs), .Data_Address(PC), .Ram_Out_0(RAM_Out_0),
    .Ram_Out_1(RAM_Out_1), .Ram_Out_2(RAM_Out_2), .Ram_Out_3(RAM_Out_3));
  Instruction_Decoder_2 instruction_decoder_1 (
    .In(cache_instruction_1_out_14), .ALU_op(instruction_decoder_1_alu_op),
    .B_selector(instruction_decoder_1_b_selector), .BC_path(instruction_decoder_1_bc_path),
    .Is_jump(instruction_decoder_1_is_jump), .LI_selector(instruction_decoder_1_li_selector),
    .CU_path(instruction_decoder_1_cu_path), .Special_selector(instruction_decoder_1_special_selector),
    .Is_push_2(instruction_decoder_1_is_push_2), .Is_sw(instruction_decoder_1_is_sw),
    .out_5(instruction_decoder_1_out_5), .out_6(instruction_decoder_1_out_6),
    .out_7(instruction_decoder_1_out_7),
    .Register_input_selector(instruction_decoder_1_register_input_selector),
    .Is_push(instruction_decoder_1_is_push), .pop_or_push(instruction_decoder_1_pop_or_push),
    .Is_rnd(instruction_decoder_1_is_rnd), .SE(instruction_decoder_1_se),
    .Destiny(instruction_decoder_1_destiny), .Is_kbd(instruction_decoder_1_is_kbd));
  Sign_Extender sign_extender_1 (
    .in_1(instruction_decoder_1_se), .Insert_Zero(put_zeros), .Immediate(sign_extender_1_immediate));
  Branch_Control_2 branch_control_1 (
    .PC(PC), .in_2(sign_extender_1_immediate), .in_3(data_path_1_jump_register),
    .in_4(instruction_decoder_1_destiny), .in_5(instruction_decoder_1_bc_path),
    .in_6(instruction_decoder_1_is_jump), .Z(data_path_1_zero), .N(data_path_1_negative),
    .out_9(branch_control_1_out_9));
  Control_Unit control_unit_1 (
    .Reset(Reset), .Clk(Clock), .Finish_IC(Finish_IC), .Finish_CD(Finish_CD),
    .Is_sw(instruction_decoder_1_is_sw), .LI_selector(instruction_decoder_1_li_selector),
    .Special_selector(instruction_decoder_1_special_selector), .CU_path(instruction_decoder_1_cu_path),
    .IC_Enable(CIE), .Put_Zeros(put_zeros),
    .Register_address_selector(control_unit_1_register_address_selector), .RF_write(control_unit_1_rf_write),
    .SP_selector_input(control_unit_1_sp_selector_input), .Is_push(instruction_decoder_1_is_push_2),
    .kbd_enable(Kbd_Enable), .tty_enable(TTY_Enable), .Sel_Cache_Ram(D_I), .Data_Write(R_W_CD),
    .Data_Write_Finish(R_W_CI), .Data_Enable(CDE), .mul_or_div(control_unit_1_mul_or_div),
    .Load_PC(control_unit_1_load_pc), .stop(Stop));
  Program_Counter program_counter_1 (
    .in_1(branch_control_1_out_9), .out_5(PC), .Enable(control_unit_1_load_pc), .CLK(Clock), .Reset(Reset));
  Data_Path data_path_1 (
    .Reset(Reset), .Clk(Clock), .Kbd_ASCII_Data(Kbd_ASCII_Data), .Kbd_Available(Kbd_Available),
    .Register_address_selector(control_unit_1_register_address_selector), .RF_Write(control_unit_1_rf_write),
    .SP_selector_input(control_unit_1_sp_selector_input), .mul_or_div(control_unit_1_mul_or_div),
    .ALU_Op(instruction_decoder_1_alu_op), .Rd(instruction_decoder_1_out_5),
    .Rt(instruction_decoder_1_out_6), .Rs(instruction_decoder_1_out_7),
    .Register_input_selector(instruction_decoder_1_register_input_selector),
    .B_selector(instruction_decoder_1_b_selector), .Is_push(instruction_decoder_1_is_push),
    .pop_or_push(instruction_decoder_1_pop_or_push), .Is_rnd(instruction_decoder_1_is_rnd),
    .Sing_Extender(sign_extender_1_immediate), .Data(Data), .Tty(TTY_ASCII_Data), .Zero(data_path_1_zero),
    .Negative(data_path_1_negative), .Data_to_CD(data_path_1_data_to_cd),
    .Address_to_CD(data_path_1_address_to_cd), .Jump_register(data_path_1_jump_register),
    .Is_kbd(instruction_decoder_1_is_kbd));
  Cache_Data cache_data_1 (
    .Data_Address(data_path_1_address_to_cd), .Ram_Out_0(RAM_Out_0), .Ram_Out_1(RAM_Out_1),
    .Ram_Out_1_2(RAM_Out_2), .Ram_Out_1_3(RAM_Out_3), .Write_Data(data_path_1_data_to_cd), .CLK(Clock),
    .in_2(CDE), .RW(R_W_CD), .in_4(Read_Time), .Reset(Reset), .in_6(Write_Time),
    .out_13(cache_data_1_out_13), .out_14(Data), .out_15(Mask), .Hit(Finish_CD), .CS(cache_data_1_cs),
    .R_W_out(nRead_Write), .RAM_Input_0(RAM_In_0), .RAM_Input_1(RAM_In_1), .RAM_Input_2(RAM_In_2),
    .RAM_Input_3(RAM_In_3), .Last_RA(cache_data_1_last_ra));
  or or_1 (Chip_Select, cache_data_1_cs, cache_instruction_1_cs);
  Multiplexer #(.width(16), .enable("false")) multiplexer_1 (
    .in0(cache_data_1_out_13), .in1(cache_instruction_1_out_13), .out(Address), .sel(D_I));

  assign Kbd_Clear = Reset;

  // Other names for the same wires on the sheet: CLK = Clock; CS = Chip_Select; KBD_AVAIL = Kbd_Available;
  //   CLR = Reset; KBD_CLR = Reset; KBD_DATA[6:0] = Kbd_ASCII_Data; RAM_A[15:0] = Address;
  //   RAM_INPUT_0[31:0] = RAM_In_0; RAM_INPUT_1[31:0] = RAM_In_1; RAM_INPUT_2[31:0] = RAM_In_2;
  //   RAM_INPUT_3[31:0] = RAM_In_3; RAM_MASK[3:0] = Mask; RAM_OUTPUT_0[31:0] = RAM_Out_0;
  //   RAM_OUTPUT_1[31:0] = RAM_Out_1; RAM_OUTPUT_2[31:0] = RAM_Out_2; RAM_OUTPUT_3[31:0] = RAM_Out_3;
  //   RW = nRead_Write; TTY_DATA[6:0] = TTY_ASCII_Data

  // Notes on the sheet:
  //   DATA FROM RAM
  //   KEYBOARD
  //   TTY
  //   SEQUENCING
  //   DATA TO RAM
  //   DATA WRITE MASK
  //   RAM TIMING
  //   RAM CONTROL
  //   RAM ADDRESS
endmodule

module Data_Path (
  input  Reset,
  input  Clk,
  input  [6:0] Kbd_ASCII_Data,
  input  Kbd_Available,
  input  Register_address_selector,
  input  RF_Write,
  input  SP_selector_input,
  input  mul_or_div,
  input  [3:0] ALU_Op,
  input  [4:0] Rd,
  input  [4:0] Rt,
  input  [4:0] Rs,
  input  [1:0] Register_input_selector,
  input  [1:0] B_selector,
  input  Is_push,
  input  pop_or_push,
  input  Is_rnd,
  input  Is_kbd,
  input  [31:0] Sing_Extender,
  input  [31:0] Data,
  output [6:0] Tty,
  output Zero,
  output Negative,
  output [31:0] Jump_register,
  output [31:0] Data_to_CD,
  output [31:0] Address_to_CD
);

  wire [1:0] multiplexer_1_out;
  wire [4:0] multiplexer_4_out, multiplexer_6_out;
  wire [31:0] alu_1_high, ALU_Result, B, bit_extender_1_out, Hi, Lo, multiplexer_2_out, multiplexer_3_out,
       multiplexer_5_out, multiplexer_7_out, multiplexer_8_out, multiplexer_9_out, random_1_out, SP;

  Multiplexer #(.width(2), .enable("false")) multiplexer_1 (
    .in0(Register_input_selector), .in1(2'b00), .out(multiplexer_1_out), .sel(SP_selector_input));
  Multiplexer #(.select(2), .width(32), .enable("false")) multiplexer_2 (
    .in0(ALU_Result), .in1(Data), .in2(Hi), .in3(Lo), .out(multiplexer_2_out), .sel(multiplexer_1_out));
  Multiplexer #(.width(32), .enable("false")) multiplexer_3 (
    .in0(multiplexer_2_out), .in1(random_1_out), .out(multiplexer_3_out), .sel(Is_rnd));
  Random #(.width(32)) random_1 (.clk(Clk), .out(random_1_out));  // open: next, clr
  Multiplexer #(.width(5), .enable("false")) multiplexer_4 (
    .in0(Rd), .in1(Rt), .out(multiplexer_4_out), .sel(Register_address_selector));
  Multiplexer #(.width(32), .enable("false")) multiplexer_5 (
    .in0({32{1'b1}}), .in1(bit_extender_1_out), .out(multiplexer_5_out), .sel(Kbd_Available));
  assign bit_extender_1_out = {{25{1'b0}}, Kbd_ASCII_Data};  // Bit_Extender bit_extender_1
  Multiplexer #(.width(5), .enable("false")) multiplexer_6 (
    .in0(multiplexer_4_out), .in1({5{1'b1}}), .out(multiplexer_6_out), .sel(SP_selector_input));
  Multiplexer #(.width(32), .enable("false")) multiplexer_7 (
    .in0(multiplexer_3_out), .in1(multiplexer_5_out), .out(multiplexer_7_out), .sel(Is_kbd));
  Register_File register_file_1 (
    .DA(multiplexer_6_out), .IN(multiplexer_7_out), .R_W(RF_Write), .SA(Rs), .SB(Rt), .Reset(Reset),
    .Clk(Clk), .A(Jump_register), .MoD(mul_or_div), .HI(alu_1_high), .LO(ALU_Result), .B(B), .out_13(SP),
    .out_14(Hi), .out_15(Lo));
  Multiplexer #(.width(32), .enable("false")) multiplexer_8 (
    .in0(Jump_register), .in1(SP), .out(multiplexer_8_out), .sel(pop_or_push));
  Multiplexer #(.select(2), .width(32), .enable("false")) multiplexer_9 (
    .in0(B), .in1(Sing_Extender), .in2(32'h4), .out(multiplexer_9_out), .sel(B_selector));  // open: in3
  ALU alu_1 (
    .in_1(multiplexer_8_out), .in_2(multiplexer_9_out), .Selector(ALU_Op), .Result(ALU_Result),
    .High(alu_1_high), .Zero(Zero), .Negative(Negative));
  Multiplexer #(.width(32), .enable("false")) multiplexer_10 (
    .in0(B), .in1(Jump_register), .out(Data_to_CD), .sel(Is_push));
  Multiplexer #(.width(32), .enable("false")) multiplexer_11 (
    .in0(ALU_Result), .in1(SP), .out(Address_to_CD), .sel(pop_or_push));

  assign Tty = Jump_register[6:0];

  // Other names for the same wires on the sheet: A[31:0] = Jump_register; kbd = Is_kbd; KBD_AVAIL = Kbd_Available;
  //   KBD_DATA[6:0] = Kbd_ASCII_Data; N = Negative; R = Reset; R_in_selector[1:0] = Register_input_selector;
  //   R_W = RF_Write; RA_selector = Register_address_selector; rnd = Is_rnd; SE[31:0] = Sing_Extender;
  //   SP_selector = SP_selector_input; Z = Zero

  // Notes on the sheet:
  //   Input
  //   Control Unit
  //   Instruction Decodder
  //   Sign Extender
  //   Cache Data
  //   Branch Control
  //   Cache Data
  //   Output
endmodule

module Register_File (
  input  [4:0] DA,
  input  [31:0] IN,
  input  R_W,
  input  [4:0] SA,
  input  [4:0] SB,
  input  Reset,
  input  Clk,
  input  MoD,
  input  [31:0] HI,
  input  [31:0] LO,
  output [31:0] A,
  output [31:0] B,
  output [31:0] out_13,
  output [31:0] out_14,
  output [31:0] out_15
);

  wire W01, W02, W03, W04, W05, W06, W07, W08, W09, W10, W11, W12, W13, W14, W15, W16, W17, W18, W19, W20,
       W21, W22, W23, W24, W25, W26, W27, W28, W29, W30, W31;
  wire [31:0] D00, D01, D02, D03, D04, D05, D06, D07, D08, D09, D10, D11, D12, D13, D14, D15, D16, D17, D18,
       D19, D20, D21, D22, D23, D24, D25, D26, D27, D28, D29, D30;

  Demultiplexer #(.select(5), .enable("false")) demultiplexer_1 (
    .out1(W01), .out2(W02), .out3(W03), .out4(W04), .out5(W05), .out6(W06), .out7(W07), .out8(W08),
    .out9(W09), .out10(W10), .out11(W11), .out12(W12), .out13(W13), .out14(W14), .out15(W15), .out16(W16),
    .out17(W17), .out18(W18), .out19(W19), .out20(W20), .out21(W21), .out22(W22), .out23(W23), .out24(W24),
    .out25(W25), .out26(W26), .out27(W27), .out28(W28), .out29(W29), .out30(W30), .out31(W31), .in(R_W),
    .sel(DA));  // open: out0
  Multiplexer #(.select(5), .width(32), .enable("false")) multiplexer_1 (
    .in0(D00), .in1(D01), .in2(D02), .in3(D03), .in4(D04), .in5(D05), .in6(D06), .in7(D07), .in8(D08),
    .in9(D09), .in10(D10), .in11(D11), .in12(D12), .in13(D13), .in14(D14), .in15(D15), .in16(D16),
    .in17(D17), .in18(D18), .in19(D19), .in20(D20), .in21(D21), .in22(D22), .in23(D23), .in24(D24),
    .in25(D25), .in26(D26), .in27(D27), .in28(D28), .in29(D29), .in30(D30), .in31(out_13), .out(A), .sel(SA));
  Multiplexer #(.select(5), .width(32), .enable("false")) multiplexer_2 (
    .in0(D00), .in1(D01), .in2(D02), .in3(D03), .in4(D04), .in5(D05), .in6(D06), .in7(D07), .in8(D08),
    .in9(D09), .in10(D10), .in11(D11), .in12(D12), .in13(D13), .in14(D14), .in15(D15), .in16(D16),
    .in17(D17), .in18(D18), .in19(D19), .in20(D20), .in21(D21), .in22(D22), .in23(D23), .in24(D24),
    .in25(D25), .in26(D26), .in27(D27), .in28(D28), .in29(D29), .in30(D30), .in31(out_13), .out(B), .sel(SB));
  Register #(.width(32)) register_1 (.D(IN), .en(1'b0), .Q(D00), .clk(Clk), .clr(Reset));
  Register #(.width(32)) register_2 (.D(IN), .en(W01), .Q(D01), .clk(Clk), .clr(Reset));
  Register #(.width(32)) register_3 (.D(IN), .en(W02), .Q(D02), .clk(Clk), .clr(Reset));
  Register #(.width(32)) register_4 (.D(IN), .en(W03), .Q(D03), .clk(Clk), .clr(Reset));
  Register #(.width(32)) register_5 (.D(IN), .en(W04), .Q(D04), .clk(Clk), .clr(Reset));
  Register #(.width(32)) register_6 (.D(IN), .en(W05), .Q(D05), .clk(Clk), .clr(Reset));
  Register #(.width(32)) register_7 (.D(IN), .en(W06), .Q(D06), .clk(Clk), .clr(Reset));
  Register #(.width(32)) register_8 (.D(IN), .en(W07), .Q(D07), .clk(Clk), .clr(Reset));
  Register #(.width(32)) register_9 (.D(IN), .en(W08), .Q(D08), .clk(Clk), .clr(Reset));
  Register #(.width(32)) register_10 (.D(IN), .en(W09), .Q(D09), .clk(Clk), .clr(Reset));
  Register #(.width(32)) register_11 (.D(IN), .en(W10), .Q(D10), .clk(Clk), .clr(Reset));
  Register #(.width(32)) register_12 (.D(IN), .en(W11), .Q(D11), .clk(Clk), .clr(Reset));
  Register #(.width(32)) register_13 (.D(IN), .en(W12), .Q(D12), .clk(Clk), .clr(Reset));
  Register #(.width(32)) register_14 (.D(IN), .en(W13), .Q(D13), .clk(Clk), .clr(Reset));
  Register #(.width(32)) register_15 (.D(IN), .en(W14), .Q(D14), .clk(Clk), .clr(Reset));
  Register #(.width(32)) register_16 (.D(IN), .en(W15), .Q(D15), .clk(Clk), .clr(Reset));
  Register #(.width(32)) register_17 (.D(IN), .en(W16), .Q(D16), .clk(Clk), .clr(Reset));
  Register #(.width(32)) register_18 (.D(IN), .en(W17), .Q(D17), .clk(Clk), .clr(Reset));
  Register #(.width(32)) register_19 (.D(IN), .en(W18), .Q(D18), .clk(Clk), .clr(Reset));
  Register #(.width(32)) register_20 (.D(IN), .en(W19), .Q(D19), .clk(Clk), .clr(Reset));
  Register #(.width(32)) register_21 (.D(IN), .en(W20), .Q(D20), .clk(Clk), .clr(Reset));
  Register #(.width(32)) register_22 (.D(IN), .en(W21), .Q(D21), .clk(Clk), .clr(Reset));
  Register #(.width(32)) register_23 (.D(IN), .en(W22), .Q(D22), .clk(Clk), .clr(Reset));
  Register #(.width(32)) register_24 (.D(IN), .en(W23), .Q(D23), .clk(Clk), .clr(Reset));
  Register #(.width(32)) register_25 (.D(IN), .en(W24), .Q(D24), .clk(Clk), .clr(Reset));
  Register #(.width(32)) register_26 (.D(IN), .en(W25), .Q(D25), .clk(Clk), .clr(Reset));
  Register #(.width(32)) register_27 (.D(IN), .en(W26), .Q(D26), .clk(Clk), .clr(Reset));
  Register #(.width(32)) register_28 (.D(IN), .en(W27), .Q(D27), .clk(Clk), .clr(Reset));
  Register #(.width(32)) register_29 (.D(IN), .en(W28), .Q(D28), .clk(Clk), .clr(Reset));
  Register #(.width(32)) register_30 (.D(IN), .en(W29), .Q(D29), .clk(Clk), .clr(Reset));
  Register #(.width(32)) register_31 (.D(IN), .en(W30), .Q(D30), .clk(Clk), .clr(Reset));
  Register #(.width(32)) register_32 (.D(IN), .en(W31), .Q(out_13), .clk(Clk), .clr(Reset));
  Register #(.width(32)) register_33 (.D(HI), .en(MoD), .Q(out_14), .clk(Clk));  // open: clr
  Register #(.width(32)) register_34 (.D(LO), .en(MoD), .Q(out_15), .clk(Clk));  // open: clr

  // Other names for the same wires on the sheet: C = Clk; D31[31:0] = out_13; Data_A[31:0] = A; Data_B[31:0] = B;
  //   HI_t[31:0] = out_14; LO_t[31:0] = out_15; R = Reset

  // Notes on the sheet:
  //   Data Address
  //   Data In
  //   Read/Write
  //   Selector A
  //   Selector B
  //   Mult or Div
  //   Input
  //   Register File
  //   Output
  //   Mult or Div
  //   Data A
  //   Data B
  //   Stack Pointer 
endmodule

module ALU (
  input  [31:0] in_1,
  input  [31:0] in_2,
  input  [3:0] Selector,
  output [31:0] Result,
  output [31:0] High,
  output Zero,
  output Negative
);

  wire comparator_1_lt, comparator_2_lt, nor_2_out;
  wire [31:0] Add, And, Hi_Div, Hi_Divu, Hi_Mult, Hi_Mulu, Lo_Div, Lo_Divu, Lo_Mult, Lo_Mulu, Nor, Or, Slt,
       Sltu, Sub, Xor;

  Adder #(.width(32)) adder_1 (.a(in_1), .b(in_2), .out(Add));  // open: cin, cout
  Subtractor #(.width(32)) subtractor_1 (.a(in_1), .b(in_2), .out(Sub));  // open: bin, bout
  assign And = in_1 & in_2;  // AND_Gate and_1, 32 bits wide
  assign Or = in_1 | in_2;  // OR_Gate or_1, 32 bits wide
  Multiplier #(.width(32)) multiplier_1 (.a(in_1), .b(in_2), .out(Lo_Mult), .cout(Hi_Mult));  // open: cin
  assign Nor = ~(in_1 | in_2);  // NOR_Gate nor_1, 32 bits wide
  assign Xor = in_1 ^ in_2;  // XOR_Gate xor_1, 32 bits wide
  Unsigned_Multiplication unsigned_multiplication_1 (.in_1(in_1), .in_2(in_2), .Lo(Lo_Mulu), .Hi(Hi_Mulu));
  Comparator #(.width(32)) comparator_1 (.a(in_1), .b(in_2), .lt(comparator_1_lt));  // open: gt, eq
  Comparator #(.width(32), .mode("unsigned")) comparator_2 (.a(in_1), .b(in_2), .lt(comparator_2_lt));  // open: gt, eq
  assign Slt = {{31{1'b0}}, comparator_1_lt};  // Bit_Extender bit_extender_1
  assign Sltu = {{31{1'b0}}, comparator_2_lt};  // Bit_Extender bit_extender_2
  Divider #(.width(32)) divider_1 (.a(in_1), .b(in_2), .out(Lo_Div), .rem(Hi_Div));  // open: upper
  Unsigned_Division unsigned_division_1 (.in_1(in_1), .in_2(in_2), .Lo(Lo_Divu), .Hi(Hi_Divu));
  Multiplexer #(.select(4), .width(32), .enable("false")) multiplexer_1 (
    .in0(Lo_Mult), .in1(Lo_Div), .in2(Lo_Mulu), .in3(Lo_Divu), .in4(Add), .in5(Sub), .in6(And), .in7(Or),
    .in8(Nor), .in9(Xor), .in10(Slt), .in11(Sltu), .in12(in_1), .out(Result), .sel(Selector));  // open: in13, in14, in15
  Multiplexer #(.select(2), .width(32)) multiplexer_2 (
    .in0(Hi_Mult), .in1(Hi_Div), .in2(Hi_Mulu), .in3(Hi_Divu), .out(High), .sel(Selector[1:0]), .en(nor_2_out));
  nor nor_2 (nor_2_out, Selector[2], Selector[3]);
  // Probe on Result
  Comparator #(.width(32)) comparator_3 (.a(Result), .b({32{1'b0}}), .eq(Zero), .lt(Negative));  // open: gt
  // Probe on Add
  // Probe on Sub
  // Probe on Lo_Mult
  // Probe on Lo_Div
  // Probe on in_1
  // Probe on in_2
  // Probe on High
  // Probe on Slt
  // Probe on Sltu
  // Probe on Lo_Mulu
  // Probe on Lo_Divu

  // Other names for the same wires on the sheet: A[31:0] = in_1; B[31:0] = in_2; N = Negative; S[3:0] = Selector;
  //   Z = Zero

  // Notes on the sheet:
  //   Input
  //   Operator A
  //   Operator B
  //   ALU
  //   Flags
  //   Output
  //   Visual
  //   Operator A
  //   Operator B
  //   Results
endmodule

module Unsigned_Multiplication (
  input  [31:0] in_1,
  input  [31:0] in_2,
  output [31:0] Lo,
  output [31:0] Hi
);

  wire [31:0] multiplexer_1_out, multiplexer_2_out, negator_1_out, negator_2_out;

  Negator #(.width(32)) negator_1 (.in(in_1), .out(negator_1_out));
  Negator #(.width(32)) negator_2 (.in(in_2), .out(negator_2_out));
  Multiplexer #(.width(32), .enable("false")) multiplexer_1 (
    .in0(in_1), .in1(negator_1_out), .out(multiplexer_1_out), .sel(in_1[31]));
  Multiplexer #(.width(32), .enable("false")) multiplexer_2 (
    .in0(in_2), .in1(negator_2_out), .out(multiplexer_2_out), .sel(in_2[31]));
  Multiplier #(.width(32)) multiplier_1 (
    .a(multiplexer_1_out), .b(multiplexer_2_out), .out(Lo), .cout(Hi));  // open: cin

  // Other names for the same wires on the sheet: SignA = in_1[31]; SignB = in_2[31]
endmodule

module Unsigned_Division (
  input  [31:0] in_1,
  input  [31:0] in_2,
  output [31:0] Lo,
  output [31:0] Hi
);

  wire [31:0] multiplexer_1_out, multiplexer_2_out, negator_1_out, negator_2_out;

  Negator #(.width(32)) negator_1 (.in(in_1), .out(negator_1_out));
  Negator #(.width(32)) negator_2 (.in(in_2), .out(negator_2_out));
  Multiplexer #(.width(32), .enable("false")) multiplexer_1 (
    .in0(in_1), .in1(negator_1_out), .out(multiplexer_1_out), .sel(in_1[31]));
  Multiplexer #(.width(32), .enable("false")) multiplexer_2 (
    .in0(in_2), .in1(negator_2_out), .out(multiplexer_2_out), .sel(in_2[31]));
  Divider #(.width(32)) divider_1 (.a(multiplexer_1_out), .b(multiplexer_2_out), .out(Lo), .rem(Hi));  // open: upper

  // Other names for the same wires on the sheet: SignA = in_1[31]; SignB = in_2[31]
endmodule

module Sign_Extender (
  input  [15:0] in_1,
  input  Insert_Zero,
  output [31:0] Immediate
);

  wire [15:0] bit_extender_1_out;

  assign bit_extender_1_out = {{15{in_1[15]}}, in_1[15]};  // Bit_Extender bit_extender_1
  Multiplexer #(.width(16), .enable("false")) multiplexer_1 (
    .in0(bit_extender_1_out), .in1({16{1'b0}}), .out(Immediate[31:16]), .sel(Insert_Zero));

  assign Immediate[15:0] = in_1;

  // Other names for the same wires on the sheet: IZ = Insert_Zero
endmodule

module Branch_Control_2 (
  input  [31:0] PC,
  input  [31:0] in_2,
  input  [31:0] in_3,
  input  [25:0] in_4,
  input  [2:0] in_5,
  input  in_6,
  input  Z,
  input  N,
  output [31:0] out_9
);

  wire and_1_out, and_2_out, and_3_out, and_4_out, and_5_out, and_7_out, comparator_1_eq, comparator_2_eq,
       comparator_3_eq, comparator_4_eq, comparator_5_eq, comparator_6_eq, comparator_7_eq, or_1_out,
       or_2_out, or_3_out;
  wire [1:0] Jump_Selector;
  wire [31:0] PC_4___OffSet_4, PC___4, shifter_1_out;

  Adder #(.width(32)) adder_1 (.a(PC), .b(32'h4), .out(PC___4));  // open: cin, cout
  Shifter #(.width(32)) shifter_1 (.in(in_2), .\dist (5'b00010), .out(shifter_1_out));
  Adder #(.width(32)) adder_2 (.a(PC___4), .b(shifter_1_out), .out(PC_4___OffSet_4));  // open: cin, cout
  Comparator #(.width(3)) comparator_1 (.a(in_5), .b(3'b000), .eq(comparator_1_eq));  // open: gt, lt
  Comparator #(.width(3)) comparator_2 (.a(3'b010), .b(in_5), .eq(comparator_2_eq));  // open: gt, lt
  Comparator #(.width(3)) comparator_3 (.a(in_5), .b(3'b100), .eq(comparator_3_eq));  // open: gt, lt
  Comparator #(.width(3)) comparator_4 (.a(3'b101), .b(in_5), .eq(comparator_4_eq));  // open: gt, lt
  Comparator #(.width(3)) comparator_5 (.a(3'b110), .b(in_5), .eq(comparator_5_eq));  // open: gt, lt
  Comparator #(.width(3)) comparator_6 (.a(3'b111), .b(in_5), .eq(comparator_6_eq));  // open: gt, lt
  Comparator #(.width(3)) comparator_7 (.a(3'b001), .b(in_5), .eq(comparator_7_eq));  // open: gt, lt
  or or_1 (or_1_out, N, Z);
  or or_2 (or_2_out, comparator_1_eq, comparator_2_eq);
  and and_1 (and_1_out, Z, comparator_3_eq);
  and and_2 (and_2_out, ~Z, comparator_4_eq);  // AND_Gate
  and and_3 (and_3_out, or_1_out, comparator_5_eq);
  and and_4 (and_4_out, ~N, ~Z, comparator_6_eq);  // AND_Gate
  and and_5 (and_5_out, N, comparator_7_eq);
  and and_6 (Jump_Selector[1], in_6, or_2_out);
  or or_3 (or_3_out, and_1_out, and_2_out, and_3_out, and_4_out, and_5_out);
  Multiplexer #(.select(2), .width(32), .enable("false")) multiplexer_1 (
    .in0(PC___4), .in1(PC_4___OffSet_4), .in2(in_3), .in3({PC[31:28], in_4, 2'b00}), .out(out_9),
    .sel(Jump_Selector));
  and and_7 (and_7_out, in_6, or_3_out);
  or or_4 (Jump_Selector[0], comparator_2_eq, and_7_out);
  // Probe on PC___4
  // Probe on PC_4___OffSet_4
  // Probe on {PC[31:28], in_4, 2'b00}
  // Probe on in_3

  // Other names for the same wires on the sheet: Destiny[25:0] = in_4; DestJmp[31:2] = {PC[31:28], in_4}; Jmp = in_6;
  //   jr[31:0] = in_3; Jump_Condition[2:0] = in_5; OffSet[31:0] = in_2; PC_prime[31:0] = out_9

  // Notes on the sheet:
  //   Input
  //   Output
  //   Branch Control
endmodule

module Program_Counter (
  input  [31:0] in_1,
  input  Enable,
  input  Reset,
  input  CLK,
  output [31:0] out_5
);

  Register #(.width(32)) register_1 (.D(in_1), .en(Enable), .Q(out_5), .clk(CLK), .clr(Reset));

  // Notes on the sheet:
  //   Input
  //   Output
  //   Program Counter
endmodule

module Control_Unit (
  input  Reset,
  input  Clk,
  input  Finish_IC,
  input  Finish_CD,
  input  Is_sw,
  input  Is_push,
  input  LI_selector,
  input  [1:0] Special_selector,
  input  [2:0] CU_path,
  output stop,
  output kbd_enable,
  output tty_enable,
  output Data_Enable,
  output Data_Write_Finish,
  output Data_Write,
  output Sel_Cache_Ram,
  output IC_Enable,
  output Register_address_selector,
  output SP_selector_input,
  output mul_or_div,
  output RF_write,
  output Put_Zeros,
  output Load_PC
);

  wire d_ff_1_q, d_ff_2_q, d_ff_3_q, d_ff_4_q, d_ff_5_q, d_ff_8_q, Data_En_0, Data_En_1, Data_En_2,
       Data_En_3, Data_Write_Finish_0, Data_Write_Finish_1, demultiplexer_1_out0, demultiplexer_1_out1,
       demultiplexer_2_out0, demultiplexer_3_out3, demultiplexer_4_out0, demultiplexer_5_out0,
       demultiplexer_6_out0, demultiplexer_7_out0, demultiplexer_8_out0, demultiplexer_9_out0,
       demultiplexer_10_out0, End_0, End_1, End_2, End_3, Erase_Last_Data_Write, inmediate, lw_or_sw,
       or_10_out, or_11_out, pop_or_push, RF_selector_1, RF_write_1, RF_write_2, RF_write_4, RF_write_5,
       RF_write_6, RF_write_7, RF_write_8, special;

  Demultiplexer #(.enable("false")) demultiplexer_1 (
    .out0(demultiplexer_1_out0), .out1(demultiplexer_1_out1), .in(lw_or_sw), .sel(Is_sw));
  or or_1 (IC_Enable, demultiplexer_4_out0, Load_PC);
  Demultiplexer #(.enable("false")) demultiplexer_2 (
    .out0(demultiplexer_2_out0), .out1(RF_write_6), .in(pop_or_push), .sel(Is_push));
  Demultiplexer #(.select(2), .enable("false")) demultiplexer_3 (
    .out0(RF_write_7), .out1(tty_enable), .out2(RF_write_8), .out3(demultiplexer_3_out3), .in(special),
    .sel(Special_selector));
  Demultiplexer #(.enable("false")) demultiplexer_4 (
    .out0(demultiplexer_4_out0), .out1(Erase_Last_Data_Write), .in(d_ff_1_q), .sel(Finish_IC));
  D_Flip_Flop d_ff_1 (.clk(Clk), .D(IC_Enable), .Q(d_ff_1_q), .preset(Reset));  // open: Qn, en, reset
  Demultiplexer #(.enable("false")) demultiplexer_5 (
    .out0(demultiplexer_5_out0), .out1(Put_Zeros), .in(inmediate), .sel(LI_selector));
  or or_2 (Data_En_0, demultiplexer_7_out0, demultiplexer_1_out0);
  or or_3 (Data_En_1, demultiplexer_8_out0, demultiplexer_1_out1);
  or or_4 (Data_En_2, demultiplexer_9_out0, demultiplexer_2_out0);
  D_Flip_Flop d_ff_2 (.clk(Clk), .D(Data_En_0), .Q(d_ff_2_q), .reset(Reset));  // open: Qn, preset, en
  D_Flip_Flop d_ff_3 (.clk(Clk), .D(Data_En_1), .Q(d_ff_3_q), .reset(Reset));  // open: Qn, preset, en
  D_Flip_Flop d_ff_4 (.clk(Clk), .D(Data_En_2), .Q(d_ff_4_q), .reset(Reset));  // open: Qn, preset, en
  D_Flip_Flop d_ff_5 (.clk(Clk), .D(RF_write_6), .Q(d_ff_5_q), .reset(Reset));  // open: Qn, preset, en
  D_Flip_Flop d_ff_6 (.clk(Clk), .D(RF_write_7), .Q(kbd_enable), .reset(Reset));  // open: Qn, preset, en
  D_Flip_Flop d_ff_7 (
    .clk(Clk), .D(demultiplexer_3_out3), .Q(stop), .en(demultiplexer_3_out3), .reset(Reset));  // open: Qn, preset
  Demultiplexer #(.select(3), .enable("false")) demultiplexer_6 (
    .out0(demultiplexer_6_out0), .out1(inmediate), .out2(mul_or_div), .out3(RF_write_1), .out4(RF_write_2),
    .out5(lw_or_sw), .out6(pop_or_push), .out7(special), .in(Erase_Last_Data_Write), .sel(CU_path));
  Demultiplexer #(.enable("false")) demultiplexer_7 (
    .out0(demultiplexer_7_out0), .out1(RF_selector_1), .in(d_ff_2_q), .sel(Finish_CD));
  Demultiplexer #(.enable("false")) demultiplexer_8 (
    .out0(demultiplexer_8_out0), .out1(Data_Write_Finish_0), .in(d_ff_3_q), .sel(Finish_CD));
  Demultiplexer #(.enable("false")) demultiplexer_9 (
    .out0(demultiplexer_9_out0), .out1(RF_write_4), .in(d_ff_4_q), .sel(Finish_CD));
  or or_5 (End_0, demultiplexer_5_out0, Put_Zeros);
  or or_6 (Data_En_3, demultiplexer_10_out0, d_ff_5_q);
  or or_7 (End_3, kbd_enable, tty_enable, RF_write_8);
  Demultiplexer #(.enable("false")) demultiplexer_10 (
    .out0(demultiplexer_10_out0), .out1(Data_Write_Finish_1), .in(d_ff_8_q), .sel(Finish_CD));
  D_Flip_Flop d_ff_8 (.clk(Clk), .D(Data_En_3), .Q(d_ff_8_q), .reset(Reset));  // open: Qn, preset, en
  or or_8 (End_1, RF_selector_1, Data_Write_Finish_0);
  D_Flip_Flop d_ff_9 (.clk(Clk), .D(RF_write_4), .Q(RF_write_5), .reset(Reset));  // open: Qn, preset, en
  or or_9 (End_2, RF_write_5, Data_Write_Finish_1);
  or or_10 (or_10_out, demultiplexer_6_out0, End_0, mul_or_div, RF_write_1, RF_write_2, End_1, End_2, End_3);
  D_Flip_Flop d_ff_10 (.clk(Clk), .D(or_10_out), .Q(Load_PC), .reset(Reset));  // open: Qn, preset, en
  or or_11 (or_11_out, Data_Write_Finish_0, Data_Write_Finish_1);
  Register #(.width(1)) register_1 (
    .D(or_11_out), .Q(Data_Write_Finish), .clk(Clk), .clr(Erase_Last_Data_Write));  // open: en
  or or_12 (Register_address_selector, inmediate, RF_selector_1);
  or or_13 (RF_write, End_0, RF_write_1, RF_write_2, RF_selector_1, RF_write_4, RF_write_5, RF_write_6, RF_write_7, RF_write_8);
  or or_14 (SP_selector_input, RF_write_5, RF_write_6);
  or or_15 (Data_Write, Data_En_1, Data_En_3);
  nor nor_1 (Sel_Cache_Ram, Data_En_0, Data_En_1, Data_En_2, Data_En_3);
  or or_16 (Data_Enable, Data_En_0, Data_En_1, Data_En_2, Data_En_3);

  // Other names for the same wires on the sheet: CD_Enable = Data_Enable;
  //   Data_Write_Finish_LastOp = Data_Write_Finish; DataWrite = Data_Write; Finish_CD_process = Finish_CD;
  //   Finish_IC_process = Finish_IC; halt = stop; RF_selector_0 = inmediate; R = Reset;
  //   Register_selector = Register_address_selector; RF_write_0 = End_0; RF_write_3 = RF_selector_1;
  //   SelCacheRam = Sel_Cache_Ram; SelCacheRam_0 = Data_En_0; Data_Write_0 = Data_En_1; SelCacheRam_1 = Data_En_1;
  //   SelCacheRam_2 = Data_En_2; Data_Write_1 = Data_En_3; SelCacheRam_3 = Data_En_3; SP_selector_0 = RF_write_5;
  //   SP_selector_1 = RF_write_6

  // Notes on the sheet:
  //   Input
  //   Cache
  //   Cache
  //   Instruction Decoder
  //   Output
  //   S-MIPS
  //   Data Path
  //   Branch Control
  //   tty
  //   rnd
  //   nop and jumps
  //   add,sub,slt,sltu,and,nor,or,xor
  //   mfhi,mflo
endmodule

module Instruction_Decoder_2 (
  input  [31:0] In,
  output [3:0] ALU_op,
  output [1:0] B_selector,
  output [1:0] Register_input_selector,
  output [4:0] out_5,
  output [4:0] out_6,
  output [4:0] out_7,
  output pop_or_push,
  output Is_push,
  output Is_rnd,
  output Is_kbd,
  output [2:0] BC_path,
  output Is_jump,
  output [25:0] Destiny,
  output Is_sw,
  output Is_push_2,
  output LI_selector,
  output [1:0] Special_selector,
  output [2:0] CU_path,
  output [15:0] SE
);

  wire a, add, add_addi, add_sub, addi, \and , and_3_out, and_5_out, and_andi, andi, beq, bgtz, blez, bltz,
       bne, comparator_2_eq, comparator_3_eq, comparator_4_eq, comparator_5_eq, comparator_6_eq,
       comparator_7_eq, comparator_8_eq, comparator_10_eq, comparator_11_eq, comparator_12_eq,
       comparator_13_eq, div, divu, halt, inmediate, jr, jump, logical_1, logical_2, lw, lw_or_sw, mfhi,
       mflo, mul, mul_or_div, mulu, nop, \nor , \or , or_ori, ori, pop, r_ops, R_type_0x0, slt, slt_slti,
       slti, sltiu, sltu, sltu_sltiu, special, sub, sub_comp, tty, \xor , xor_xori, xori;
  wire [1:0] HI_selector;
  wire [2:0] bit_extender_1_out;

  Comparator #(.width(6)) comparator_1 (.a(In[31:26]), .b({6{1'b0}}), .eq(R_type_0x0));  // open: gt, lt
  Comparator #(.width(6)) comparator_2 (.a({6{1'b1}}), .b(In[5:0]), .eq(comparator_2_eq));  // open: gt, lt
  nor nor_1 (nop, In[31], In[30], In[29], In[28], In[27], In[26], In[25], In[24], In[23], In[22], In[21], In[20], In[19], In[18], In[17], In[16], In[14], In[13], In[12], In[11], In[10], In[9], In[8], In[7], In[6], In[5], In[4], In[3], In[2], In[1], In[0], In[15]);
  Comparator #(.width(4)) comparator_3 (.a(In[5:2]), .b(4'b1000), .eq(comparator_3_eq));  // open: gt, lt
  Comparator #(.width(4)) comparator_4 (.a(In[5:2]), .b(4'b1001), .eq(comparator_4_eq));  // open: gt, lt
  and and_1 (mul_or_div, R_type_0x0, comparator_5_eq);
  Comparator #(.width(4)) comparator_5 (.a(In[5:2]), .b(4'b0110), .eq(comparator_5_eq));  // open: gt, lt
  and and_2 (logical_2, R_type_0x0, comparator_6_eq);
  Comparator #(.width(4)) comparator_6 (.a(In[5:2]), .b(4'b1010), .eq(comparator_6_eq));  // open: gt, lt
  and and_3 (and_3_out, R_type_0x0, comparator_7_eq);
  Comparator #(.width(4)) comparator_7 (.a(In[5:2]), .b(4'b0100), .eq(comparator_7_eq));  // open: gt, lt
  and and_4 (jr, R_type_0x0, comparator_8_eq);
  Comparator #(.width(6)) comparator_8 (.a(In[5:0]), .b(6'b001000), .eq(comparator_8_eq));  // open: gt, lt
  Comparator #(.width(6)) comparator_9 (.a(In[31:26]), .b({6{1'b1}}), .eq(special));  // open: gt, lt
  and and_5 (and_5_out, special, comparator_10_eq);
  Comparator #(.width(3)) comparator_10 (.a(In[5:3]), .b(3'b000), .eq(comparator_10_eq));  // open: gt, lt
  and and_6 (halt, special, comparator_2_eq);
  Comparator #(.width(6)) comparator_11 (.a(In[31:26]), .b(6'b111000), .eq(comparator_11_eq));  // open: gt, lt
  and and_7 (B_selector[1], comparator_11_eq, comparator_12_eq);
  Comparator #(.width(5)) comparator_12 (.a(In[5:1]), .b({5{1'b0}}), .eq(comparator_12_eq));  // open: gt, lt
  and and_8 (add_sub, R_type_0x0, comparator_3_eq);
  and and_9 (logical_1, R_type_0x0, comparator_4_eq);
  Demultiplexer #(.select(2), .enable("false")) demultiplexer_1 (
    .out0(mul), .out1(mulu), .out2(div), .out3(divu), .in(mul_or_div), .sel(In[1:0]));
  Demultiplexer #(.select(2), .enable("false")) demultiplexer_2 (
    .out0(\xor ), .out2(slt), .out3(sltu), .in(logical_2), .sel(In[1:0]));  // open: out1
  Demultiplexer #(.select(2), .enable("false")) demultiplexer_3 (
    .out0(mfhi), .out2(mflo), .in(and_3_out), .sel(In[1:0]));  // open: out1, out3
  Demultiplexer #(.select(3), .enable("false")) demultiplexer_4 (
    .out1(tty), .out2(Is_rnd), .out4(Is_kbd), .in(and_5_out), .sel(In[2:0]));  // open: out0, out3, out5, out6, out7
  Demultiplexer #(.enable("false")) demultiplexer_5 (.out0(pop), .out1(Is_push), .in(B_selector[1]), .sel(In[0]));
  Demultiplexer #(.select(2), .enable("false")) demultiplexer_6 (
    .out0(add), .out2(sub), .in(add_sub), .sel(In[1:0]));  // open: out1, out3
  Demultiplexer #(.select(2), .enable("false")) demultiplexer_7 (
    .out0(\and ), .out1(\or ), .out3(\nor ), .in(logical_1), .sel(In[1:0]));  // open: out2
  or or_1 (slt_slti, slt, slti);
  or or_2 (sltu_sltiu, sltu, sltiu);
  or or_3 (LI_selector, andi, ori, xori);
  or or_4 (a, blez, bgtz, bltz);
  or or_5 (sub_comp, bne, sub, Is_push, beq);
  or or_6 (B_selector[0], inmediate, lw_or_sw);
  or or_7 (r_ops, add_sub, logical_1, logical_2);
  or or_8 (Register_input_selector[0], mflo, pop, lw);
  or or_9 (Register_input_selector[1], mfhi, mflo);
  or or_10 (Special_selector[0], tty, halt);
  or or_11 (Special_selector[1], Is_rnd, halt);
  Comparator #(.width(3)) comparator_13 (.a(In[31:29]), .b(3'b000), .eq(comparator_13_eq));  // open: gt, lt
  Comparator #(.width(3)) comparator_14 (.a(In[31:29]), .b(3'b001), .eq(inmediate));  // open: gt, lt
  Comparator #(.width(5)) comparator_15 (.a({In[31:30], In[28:26]}), .b(5'b10011), .eq(lw_or_sw));  // open: gt, lt
  Demultiplexer #(.select(3), .enable("false")) demultiplexer_8 (
    .out1(bltz), .out4(beq), .out5(bne), .out6(blez), .out7(bgtz), .in(comparator_13_eq), .sel(In[28:26]));  // open: out0, out2, out3
  Demultiplexer #(.select(3), .enable("false")) demultiplexer_9 (
    .out0(addi), .out2(slti), .out3(sltiu), .out4(andi), .out5(ori), .out6(xori), .in(inmediate),
    .sel(In[28:26]));  // open: out1, out7
  Demultiplexer #(.enable("false")) demultiplexer_10 (.out0(lw), .out1(Is_sw), .in(lw_or_sw), .sel(In[29]));
  or or_12 (and_andi, \and , andi);
  or or_13 (or_ori, \or , ori);
  or or_14 (xor_xori, \xor , xori);
  or or_15 (add_addi, lw, add, pop, addi, Is_sw);
  or or_16 (HI_selector[0], mulu, divu);
  or or_17 (HI_selector[1], divu, div);
  or or_18 (ALU_op[0], sub_comp, div, divu, or_ori, xor_xori, sltu_sltiu);
  or or_19 (CU_path[0], special, inmediate, lw_or_sw, r_ops);
  Comparator #(.width(6)) comparator_16 (.a(In[31:26]), .b(6'b000010), .eq(jump));  // open: gt, lt
  or or_20 (Is_jump, bltz, bne, jump, jr, bgtz, blez, beq);
  assign bit_extender_1_out = {{2{Is_jump}}, Is_jump};  // Bit_Extender bit_extender_1
  // Probe on bit_extender_1_out
  or or_21 (ALU_op[1], mulu, divu, and_andi, or_ori, slt_slti, sltu_sltiu);
  or or_22 (ALU_op[2], add_addi, or_ori, sub_comp, a, and_andi);
  or or_23 (CU_path[2], special, mfhi, B_selector[1], mflo, lw_or_sw);
  assign BC_path = In[28:26] & bit_extender_1_out;  // AND_Gate and_10, 3 bits wide
  or or_24 (ALU_op[3], \nor , xor_xori, slt_slti, sltu_sltiu, a);
  or or_25 (CU_path[1], mul_or_div, r_ops, B_selector[1], special);

  assign Destiny = In[25:0];
  assign Is_push_2 = Is_push;
  assign out_5 = In[15:11];
  assign out_6 = In[20:16];
  assign out_7 = In[25:21];
  assign pop_or_push = B_selector[1];
  assign SE = In[15:0];

  // Other names for the same wires on the sheet: Instruction[31:0] = In; Op_Code[5:0] = In[31:26];
  //   Func_Code[5:0] = In[5:0]; X[4:0] = In[10:6]; Rd[4:0] = In[15:11]; Rt[4:0] = In[20:16]; Rs[4:0] = In[25:21];
  //   kbd = Is_kbd; push = Is_push; R_in_selector[1:0] = Register_input_selector; rnd = Is_rnd; sw = Is_sw

  // Notes on the sheet:
  //   Input
  //   Intruction
  //   Output
  //   Data Path
  //   Branch Control
  //   Control Unit
  //   Sign Extender
  //   Instruction Decoder
  //   001000
  //   111111
  //   R-Type
  //   100000
  //   100010
  //   101100
  //   101101
  //   101111
  //   011000
  //   011001
  //   011010
  //   011011
  //   101000
  //   101010
  //   101011
  //   010000
  //   010010
  //   000001
  //   000010
  //   000100
  //   000000
  //   000001
  //   I-Type
  //   100011
  //   101011
  //   000001
  //   000100
  //   000101
  //   000110
  //   000111
  //   001000
  //   001010
  //   001011
  //   001100
  //   001101
  //   001110
  //   J-Type
  //   cambiar aqui (unir mas r ops)
  //   000010
endmodule

module Cache_Instruction (
  input  CLK,
  input  in_2,
  input  RW,
  input  [3:0] in_4,
  input  Reset,
  input  [31:0] Data_Address,
  input  [31:0] Ram_Out_0,
  input  [31:0] Ram_Out_1,
  input  [31:0] Ram_Out_2,
  input  [31:0] Ram_Out_3,
  input  [15:0] Last_Ram_Address,
  output out_12,
  output [15:0] out_13,
  output [31:0] out_14,
  output CS
);

  wire and_2_out, and_3_out, comparator_1_eq, comparator_2_eq, comparator_3_eq, CS_t, d_ff_1_q, Enable,
       Line0, Line1, Line2, Line3, Line4, Line5, Line6, Line7, or_1_out, Valid, Valid0, Valid1, Valid2,
       Valid3, Valid4, Valid5, Valid6, Valid7, ValidOut, ValidOut_Ram;
  wire [2:0] multiplexer_1_out;
  wire [3:0] adder_1_out, counter_1_q;
  wire [12:0] Tag0, Tag1, Tag2, Tag3, Tag4, Tag5, Tag6, Tag7, TagOut, TagOut_Ram;
  wire [31:0] Data0, Data1, Data2, Data3, Data4, Data5, Data6, Data7, Data8, Data9, Data10, Data11, Data12,
       Data13, Data14, Data15, Data16, Data17, Data18, Data19, Data20, Data21, Data22, Data23, Data24,
       Data25, Data26, Data27, Data28, Data29, Data30, Data31, multiplexer_4_out, multiplexer_5_out,
       multiplexer_6_out, multiplexer_7_out;

  and and_1 (CS, ~Reset, in_2, CS_t);  // AND_Gate
  or or_1 (or_1_out, Enable, ~Valid);  // OR_Gate
  Register #(.width(13)) register_1 (.D(Data_Address[19:7]), .en(Line0), .Q(Tag0), .clk(CLK), .clr(Reset));
  Register #(.width(13)) register_2 (.D(Data_Address[19:7]), .en(Line1), .Q(Tag1), .clk(CLK), .clr(Reset));
  Register #(.width(13)) register_3 (.D(Data_Address[19:7]), .en(Line2), .Q(Tag2), .clk(CLK), .clr(Reset));
  Register #(.width(13)) register_4 (.D(Data_Address[19:7]), .en(Line3), .Q(Tag3), .clk(CLK), .clr(Reset));
  Register #(.width(13)) register_5 (.D(Data_Address[19:7]), .en(Line4), .Q(Tag4), .clk(CLK), .clr(Reset));
  Register #(.width(13)) register_6 (.D(Data_Address[19:7]), .en(Line5), .Q(Tag5), .clk(CLK), .clr(Reset));
  Register #(.width(13)) register_7 (.D(Data_Address[19:7]), .en(Line6), .Q(Tag6), .clk(CLK), .clr(Reset));
  Register #(.width(13)) register_8 (.D(Data_Address[19:7]), .en(Line7), .Q(Tag7), .clk(CLK), .clr(Reset));
  Demultiplexer #(.select(3), .enable("false")) demultiplexer_1 (
    .out0(Line0), .out1(Line1), .out2(Line2), .out3(Line3), .out4(Line4), .out5(Line5), .out6(Line6),
    .out7(Line7), .in(and_2_out), .sel(multiplexer_1_out));
  and and_2 (and_2_out, or_1_out, in_2);
  Multiplexer #(.width(3), .enable("false")) multiplexer_1 (
    .in0(Data_Address[6:4]), .in1(Last_Ram_Address[2:0]), .out(multiplexer_1_out), .sel(RW));
  Register #(.width(32)) register_9 (.D(Ram_Out_0), .en(Line0), .Q(Data0), .clk(CLK), .clr(Reset));
  Register #(.width(32)) register_10 (.D(Ram_Out_0), .en(Line1), .Q(Data4), .clk(CLK), .clr(Reset));
  Register #(.width(32)) register_11 (.D(Ram_Out_0), .en(Line2), .Q(Data8), .clk(CLK), .clr(Reset));
  Register #(.width(32)) register_12 (.D(Ram_Out_0), .en(Line3), .Q(Data12), .clk(CLK), .clr(Reset));
  Register #(.width(32)) register_13 (.D(Ram_Out_0), .en(Line4), .Q(Data16), .clk(CLK), .clr(Reset));
  Register #(.width(32)) register_14 (.D(Ram_Out_0), .en(Line5), .Q(Data20), .clk(CLK), .clr(Reset));
  Register #(.width(32)) register_15 (.D(Ram_Out_0), .en(Line6), .Q(Data24), .clk(CLK), .clr(Reset));
  Register #(.width(32)) register_16 (.D(Ram_Out_0), .en(Line7), .Q(Data28), .clk(CLK), .clr(Reset));
  not not_1 (CS_t, out_12);
  Register #(.width(32)) register_17 (.D(Ram_Out_1), .en(Line0), .Q(Data1), .clk(CLK), .clr(Reset));
  Register #(.width(32)) register_18 (.D(Ram_Out_1), .en(Line1), .Q(Data5), .clk(CLK), .clr(Reset));
  Register #(.width(32)) register_19 (.D(Ram_Out_1), .en(Line2), .Q(Data9), .clk(CLK), .clr(Reset));
  Register #(.width(32)) register_20 (.D(Ram_Out_1), .en(Line3), .Q(Data13), .clk(CLK), .clr(Reset));
  Register #(.width(32)) register_21 (.D(Ram_Out_1), .en(Line4), .Q(Data17), .clk(CLK), .clr(Reset));
  Register #(.width(32)) register_22 (.D(Ram_Out_1), .en(Line5), .Q(Data21), .clk(CLK), .clr(Reset));
  Register #(.width(32)) register_23 (.D(Ram_Out_1), .en(Line6), .Q(Data25), .clk(CLK), .clr(Reset));
  Register #(.width(32)) register_24 (.D(Ram_Out_1), .en(Line7), .Q(Data29), .clk(CLK), .clr(Reset));
  Adder #(.width(4)) adder_1 (.a(in_4), .b(4'b0001), .out(adder_1_out));  // open: cin, cout
  D_Flip_Flop d_ff_1 (.clk(CLK), .D(CS_t), .Q(d_ff_1_q));  // open: Qn, preset, en, reset
  Comparator #(.width(13)) comparator_1 (
    .a(TagOut_Ram), .b(Last_Ram_Address[15:3]), .eq(comparator_1_eq));  // open: gt, lt
  Counter #(.width(4), .max('hf)) counter_1 (
    .load(CS_t), .D(adder_1_out), .count(d_ff_1_q), .Q(counter_1_q), .clk(CLK));  // open: carry, clr
  Comparator #(.width(13)) comparator_2 (.a(TagOut), .b(Data_Address[19:7]), .eq(comparator_2_eq));  // open: gt, lt
  and and_3 (and_3_out, ValidOut_Ram, comparator_1_eq);
  Register #(.width(32)) register_25 (.D(Ram_Out_2), .en(Line0), .Q(Data2), .clk(CLK), .clr(Reset));
  Register #(.width(32)) register_26 (.D(Ram_Out_2), .en(Line1), .Q(Data6), .clk(CLK), .clr(Reset));
  Register #(.width(32)) register_27 (.D(Ram_Out_2), .en(Line2), .Q(Data10), .clk(CLK), .clr(Reset));
  Register #(.width(32)) register_28 (.D(Ram_Out_2), .en(Line3), .Q(Data14), .clk(CLK), .clr(Reset));
  Register #(.width(32)) register_29 (.D(Ram_Out_2), .en(Line4), .Q(Data18), .clk(CLK), .clr(Reset));
  Register #(.width(32)) register_30 (.D(Ram_Out_2), .en(Line5), .Q(Data22), .clk(CLK), .clr(Reset));
  Register #(.width(32)) register_31 (.D(Ram_Out_2), .en(Line6), .Q(Data26), .clk(CLK), .clr(Reset));
  Register #(.width(32)) register_32 (.D(Ram_Out_2), .en(Line7), .Q(Data30), .clk(CLK), .clr(Reset));
  Comparator #(.width(4)) comparator_3 (.a(counter_1_q), .b(4'b0000), .eq(comparator_3_eq));  // open: gt, lt
  and and_4 (out_12, ValidOut, comparator_2_eq);
  nand nand_1 (Valid, and_3_out, RW);
  and and_5 (Enable, comparator_3_eq, d_ff_1_q);
  Register #(.width(32)) register_33 (.D(Ram_Out_3), .en(Line0), .Q(Data3), .clk(CLK), .clr(Reset));
  Register #(.width(32)) register_34 (.D(Ram_Out_3), .en(Line1), .Q(Data7), .clk(CLK), .clr(Reset));
  Register #(.width(32)) register_35 (.D(Ram_Out_3), .en(Line2), .Q(Data11), .clk(CLK), .clr(Reset));
  Register #(.width(32)) register_36 (.D(Ram_Out_3), .en(Line3), .Q(Data15), .clk(CLK), .clr(Reset));
  Register #(.width(32)) register_37 (.D(Ram_Out_3), .en(Line4), .Q(Data19), .clk(CLK), .clr(Reset));
  Register #(.width(32)) register_38 (.D(Ram_Out_3), .en(Line5), .Q(Data23), .clk(CLK), .clr(Reset));
  Register #(.width(32)) register_39 (.D(Ram_Out_3), .en(Line6), .Q(Data27), .clk(CLK), .clr(Reset));
  Register #(.width(32)) register_40 (.D(Ram_Out_3), .en(Line7), .Q(Data31), .clk(CLK), .clr(Reset));
  Register #(.width(1)) register_41 (.D(Valid), .en(Line0), .Q(Valid0), .clk(CLK), .clr(Reset));
  Register #(.width(1)) register_42 (.D(Valid), .en(Line1), .Q(Valid1), .clk(CLK), .clr(Reset));
  Register #(.width(1)) register_43 (.D(Valid), .en(Line2), .Q(Valid2), .clk(CLK), .clr(Reset));
  Register #(.width(1)) register_44 (.D(Valid), .en(Line3), .Q(Valid3), .clk(CLK), .clr(Reset));
  Register #(.width(1)) register_45 (.D(Valid), .en(Line4), .Q(Valid4), .clk(CLK), .clr(Reset));
  Register #(.width(1)) register_46 (.D(Valid), .en(Line5), .Q(Valid5), .clk(CLK), .clr(Reset));
  Register #(.width(1)) register_47 (.D(Valid), .en(Line6), .Q(Valid6), .clk(CLK), .clr(Reset));
  Register #(.width(1)) register_48 (.D(Valid), .en(Line7), .Q(Valid7), .clk(CLK), .clr(Reset));
  Multiplexer #(.select(3), .enable("false")) multiplexer_2 (
    .in0(Valid0), .in1(Valid1), .in2(Valid2), .in3(Valid3), .in4(Valid4), .in5(Valid5), .in6(Valid6),
    .in7(Valid7), .out(ValidOut), .sel(Data_Address[6:4]));
  Multiplexer #(.select(3), .width(13), .enable("false")) multiplexer_3 (
    .in0(Tag0), .in1(Tag1), .in2(Tag2), .in3(Tag3), .in4(Tag4), .in5(Tag5), .in6(Tag6), .in7(Tag7),
    .out(TagOut), .sel(Data_Address[6:4]));
  Multiplexer #(.select(3), .width(32), .enable("false")) multiplexer_4 (
    .in0(Data0), .in1(Data4), .in2(Data8), .in3(Data12), .in4(Data16), .in5(Data20), .in6(Data24),
    .in7(Data28), .out(multiplexer_4_out), .sel(Data_Address[6:4]));
  Multiplexer #(.select(3), .width(32), .enable("false")) multiplexer_5 (
    .in0(Data1), .in1(Data5), .in2(Data9), .in3(Data13), .in4(Data17), .in5(Data21), .in6(Data25),
    .in7(Data29), .out(multiplexer_5_out), .sel(Data_Address[6:4]));
  Multiplexer #(.select(3), .width(32), .enable("false")) multiplexer_6 (
    .in0(Data2), .in1(Data6), .in2(Data10), .in3(Data14), .in4(Data18), .in5(Data22), .in6(Data26),
    .in7(Data30), .out(multiplexer_6_out), .sel(Data_Address[6:4]));
  Multiplexer #(.select(3), .width(32), .enable("false")) multiplexer_7 (
    .in0(Data3), .in1(Data7), .in2(Data11), .in3(Data15), .in4(Data19), .in5(Data23), .in6(Data27),
    .in7(Data31), .out(multiplexer_7_out), .sel(Data_Address[6:4]));
  Multiplexer #(.select(3), .enable("false")) multiplexer_8 (
    .in0(Valid0), .in1(Valid1), .in2(Valid2), .in3(Valid3), .in4(Valid4), .in5(Valid5), .in6(Valid6),
    .in7(Valid7), .out(ValidOut_Ram), .sel(Last_Ram_Address[2:0]));
  Multiplexer #(.select(3), .width(13), .enable("false")) multiplexer_9 (
    .in0(Tag0), .in1(Tag1), .in2(Tag2), .in3(Tag3), .in4(Tag4), .in5(Tag5), .in6(Tag6), .in7(Tag7),
    .out(TagOut_Ram), .sel(Last_Ram_Address[2:0]));
  Multiplexer #(.select(2), .width(32), .enable("false")) multiplexer_10 (
    .in0(multiplexer_4_out), .in1(multiplexer_5_out), .in2(multiplexer_6_out), .in3(multiplexer_7_out),
    .out({out_14[7:0], out_14[15:8], out_14[23:16], out_14[31:24]}), .sel(Data_Address[3:2]));

  assign out_13 = Data_Address[19:4];

  // Other names for the same wires on the sheet: CacheEnable = in_2; OffSet[1:0] = Data_Address[3:2];
  //   Line[2:0] = Data_Address[6:4]; RamAddress[15:0] = Data_Address[19:4]; Tag[12:0] = Data_Address[19:7];
  //   Data_Out[31:0] = out_14; Hit = out_12; RamLine[2:0] = Last_Ram_Address[2:0];
  //   RamTag[12:0] = Last_Ram_Address[15:3]; R = Reset; R_W = RW; Read_Time[3:0] = in_4; RO0[31:0] = Ram_Out_0;
  //   RO1[31:0] = Ram_Out_1; RO2[31:0] = Ram_Out_2; RO3[31:0] = Ram_Out_3

  // Notes on the sheet:
  //   Output
  //   Input
endmodule

module Cache_Data (
  input  CLK,
  input  in_2,
  input  RW,
  input  [3:0] in_4,
  input  Reset,
  input  [3:0] in_6,
  input  [31:0] Data_Address,
  input  [31:0] Ram_Out_0,
  input  [31:0] Ram_Out_1,
  input  [31:0] Ram_Out_1_2,
  input  [31:0] Ram_Out_1_3,
  input  [31:0] Write_Data,
  output [15:0] out_13,
  output [31:0] out_14,
  output [3:0] out_15,
  output Hit,
  output CS,
  output R_W_out,
  output [31:0] RAM_Input_0,
  output [31:0] RAM_Input_1,
  output [31:0] RAM_Input_2,
  output [31:0] RAM_Input_3,
  output [15:0] Last_RA
);

  wire and_2_out, and_3_out, and_4_out, comparator_1_eq, CS_t, Finish_Read, Line0, Line1, Line2, Line3,
       Line4, Line5, Line6, Line7, or_1_out, or_2_out, Read, Valid, Valid0, Valid1, Valid2, Valid3, Valid4,
       Valid5, Valid6, Valid7, ValidOut;
  wire [12:0] Tag0, Tag1, Tag2, Tag3, Tag4, Tag5, Tag6, Tag7, TagOut;
  wire [31:0] Data0, Data1, Data2, Data3, Data4, Data5, Data6, Data7, Data8, Data9, Data10, Data11, Data12,
       Data13, Data14, Data15, Data16, Data17, Data18, Data19, Data20, Data21, Data22, Data23, Data24,
       Data25, Data26, Data27, Data28, Data29, Data30, Data31, multiplexer_1_out, multiplexer_2_out,
       multiplexer_3_out, multiplexer_4_out;

  and and_1 (CS, ~Reset, in_2, CS_t);  // AND_Gate
  Register #(.width(16)) register_1 (.D(Data_Address[19:4]), .en(R_W_out), .Q(Last_RA), .clk(CLK));  // open: clr
  Register #(.width(13)) register_2 (.D(Data_Address[19:7]), .en(Line0), .Q(Tag0), .clk(CLK), .clr(Reset));
  Register #(.width(13)) register_3 (.D(Data_Address[19:7]), .en(Line1), .Q(Tag1), .clk(CLK), .clr(Reset));
  Register #(.width(13)) register_4 (.D(Data_Address[19:7]), .en(Line2), .Q(Tag2), .clk(CLK), .clr(Reset));
  Register #(.width(13)) register_5 (.D(Data_Address[19:7]), .en(Line3), .Q(Tag3), .clk(CLK), .clr(Reset));
  Register #(.width(13)) register_6 (.D(Data_Address[19:7]), .en(Line4), .Q(Tag4), .clk(CLK), .clr(Reset));
  Register #(.width(13)) register_7 (.D(Data_Address[19:7]), .en(Line5), .Q(Tag5), .clk(CLK), .clr(Reset));
  Register #(.width(13)) register_8 (.D(Data_Address[19:7]), .en(Line6), .Q(Tag6), .clk(CLK), .clr(Reset));
  Register #(.width(13)) register_9 (.D(Data_Address[19:7]), .en(Line7), .Q(Tag7), .clk(CLK), .clr(Reset));
  Write_to_RAM write_to_ram_1 (
    .Write_Data(Write_Data), .OffSet(Data_Address[3:2]), .RAM_Input_0(RAM_Input_0),
    .RAM_Input_2(RAM_Input_2), .RAM_Input_1(RAM_Input_1), .RAM_Input_3(RAM_Input_3), .Mask(out_15), .RW(RW));
  Control_CD control_cd_1 (
    .CLK(CLK), .RW(RW), .Enable(in_2), .Read_Time(in_4), .Write_Time(in_6), .Read(Read), .Write(R_W_out),
    .Finish_Read(Finish_Read), .Valid(Valid), .CS(CS_t));
  Register #(.width(32)) register_10 (.D(Ram_Out_0), .en(Line0), .Q(Data0), .clk(CLK), .clr(Reset));
  Register #(.width(32)) register_11 (.D(Ram_Out_0), .en(Line1), .Q(Data4), .clk(CLK), .clr(Reset));
  Register #(.width(32)) register_12 (.D(Ram_Out_0), .en(Line2), .Q(Data8), .clk(CLK), .clr(Reset));
  Register #(.width(32)) register_13 (.D(Ram_Out_0), .en(Line3), .Q(Data12), .clk(CLK), .clr(Reset));
  Register #(.width(32)) register_14 (.D(Ram_Out_0), .en(Line4), .Q(Data16), .clk(CLK), .clr(Reset));
  Register #(.width(32)) register_15 (.D(Ram_Out_0), .en(Line5), .Q(Data20), .clk(CLK), .clr(Reset));
  Register #(.width(32)) register_16 (.D(Ram_Out_0), .en(Line6), .Q(Data24), .clk(CLK), .clr(Reset));
  Register #(.width(32)) register_17 (.D(Ram_Out_0), .en(Line7), .Q(Data28), .clk(CLK), .clr(Reset));
  Register #(.width(32)) register_18 (.D(Ram_Out_1), .en(Line0), .Q(Data1), .clk(CLK), .clr(Reset));
  Register #(.width(32)) register_19 (.D(Ram_Out_1), .en(Line1), .Q(Data5), .clk(CLK), .clr(Reset));
  Register #(.width(32)) register_20 (.D(Ram_Out_1), .en(Line2), .Q(Data9), .clk(CLK), .clr(Reset));
  Register #(.width(32)) register_21 (.D(Ram_Out_1), .en(Line3), .Q(Data13), .clk(CLK), .clr(Reset));
  Register #(.width(32)) register_22 (.D(Ram_Out_1), .en(Line4), .Q(Data17), .clk(CLK), .clr(Reset));
  Register #(.width(32)) register_23 (.D(Ram_Out_1), .en(Line5), .Q(Data21), .clk(CLK), .clr(Reset));
  Register #(.width(32)) register_24 (.D(Ram_Out_1), .en(Line6), .Q(Data25), .clk(CLK), .clr(Reset));
  Register #(.width(32)) register_25 (.D(Ram_Out_1), .en(Line7), .Q(Data29), .clk(CLK), .clr(Reset));
  Register #(.width(32)) register_26 (.D(Ram_Out_1_2), .en(Line0), .Q(Data2), .clk(CLK), .clr(Reset));
  Register #(.width(32)) register_27 (.D(Ram_Out_1_2), .en(Line1), .Q(Data6), .clk(CLK), .clr(Reset));
  Register #(.width(32)) register_28 (.D(Ram_Out_1_2), .en(Line2), .Q(Data10), .clk(CLK), .clr(Reset));
  Register #(.width(32)) register_29 (.D(Ram_Out_1_2), .en(Line3), .Q(Data14), .clk(CLK), .clr(Reset));
  Register #(.width(32)) register_30 (.D(Ram_Out_1_2), .en(Line4), .Q(Data18), .clk(CLK), .clr(Reset));
  Register #(.width(32)) register_31 (.D(Ram_Out_1_2), .en(Line5), .Q(Data22), .clk(CLK), .clr(Reset));
  Register #(.width(32)) register_32 (.D(Ram_Out_1_2), .en(Line6), .Q(Data26), .clk(CLK), .clr(Reset));
  Register #(.width(32)) register_33 (.D(Ram_Out_1_2), .en(Line7), .Q(Data30), .clk(CLK), .clr(Reset));
  or or_1 (or_1_out, Finish_Read, R_W_out);
  Comparator #(.width(13)) comparator_1 (.a(TagOut), .b(Data_Address[19:7]), .eq(comparator_1_eq));  // open: gt, lt
  Demultiplexer #(.select(3), .enable("false")) demultiplexer_1 (
    .out0(Line0), .out1(Line1), .out2(Line2), .out3(Line3), .out4(Line4), .out5(Line5), .out6(Line6),
    .out7(Line7), .in(and_2_out), .sel(Data_Address[6:4]));
  and and_2 (and_2_out, or_1_out, in_2);
  Register #(.width(32)) register_34 (.D(Ram_Out_1_3), .en(Line0), .Q(Data3), .clk(CLK), .clr(Reset));
  Register #(.width(32)) register_35 (.D(Ram_Out_1_3), .en(Line1), .Q(Data7), .clk(CLK), .clr(Reset));
  Register #(.width(32)) register_36 (.D(Ram_Out_1_3), .en(Line2), .Q(Data11), .clk(CLK), .clr(Reset));
  Register #(.width(32)) register_37 (.D(Ram_Out_1_3), .en(Line3), .Q(Data15), .clk(CLK), .clr(Reset));
  Register #(.width(32)) register_38 (.D(Ram_Out_1_3), .en(Line4), .Q(Data19), .clk(CLK), .clr(Reset));
  Register #(.width(32)) register_39 (.D(Ram_Out_1_3), .en(Line5), .Q(Data23), .clk(CLK), .clr(Reset));
  Register #(.width(32)) register_40 (.D(Ram_Out_1_3), .en(Line6), .Q(Data27), .clk(CLK), .clr(Reset));
  Register #(.width(32)) register_41 (.D(Ram_Out_1_3), .en(Line7), .Q(Data31), .clk(CLK), .clr(Reset));
  and and_3 (and_3_out, ValidOut, comparator_1_eq);
  and and_4 (and_4_out, and_3_out, or_2_out);
  or or_2 (or_2_out, ~RW, Read);  // OR_Gate
  D_Flip_Flop d_ff_1 (.clk(CLK), .D(and_4_out), .Q(Hit));  // open: Qn, preset, en, reset
  Register #(.width(1)) register_42 (.D(Valid), .en(Line0), .Q(Valid0), .clk(CLK), .clr(Reset));
  Register #(.width(1)) register_43 (.D(Valid), .en(Line1), .Q(Valid1), .clk(CLK), .clr(Reset));
  Register #(.width(1)) register_44 (.D(Valid), .en(Line2), .Q(Valid2), .clk(CLK), .clr(Reset));
  Register #(.width(1)) register_45 (.D(Valid), .en(Line3), .Q(Valid3), .clk(CLK), .clr(Reset));
  Register #(.width(1)) register_46 (.D(Valid), .en(Line4), .Q(Valid4), .clk(CLK), .clr(Reset));
  Register #(.width(1)) register_47 (.D(Valid), .en(Line5), .Q(Valid5), .clk(CLK), .clr(Reset));
  Register #(.width(1)) register_48 (.D(Valid), .en(Line6), .Q(Valid6), .clk(CLK), .clr(Reset));
  Register #(.width(1)) register_49 (.D(Valid), .en(Line7), .Q(Valid7), .clk(CLK), .clr(Reset));
  Multiplexer #(.select(3), .width(32), .enable("false")) multiplexer_1 (
    .in0(Data0), .in1(Data4), .in2(Data8), .in3(Data12), .in4(Data16), .in5(Data20), .in6(Data24),
    .in7(Data28), .out(multiplexer_1_out), .sel(Data_Address[6:4]));
  Multiplexer #(.select(3), .width(32), .enable("false")) multiplexer_2 (
    .in0(Data1), .in1(Data5), .in2(Data9), .in3(Data13), .in4(Data17), .in5(Data21), .in6(Data25),
    .in7(Data29), .out(multiplexer_2_out), .sel(Data_Address[6:4]));
  Multiplexer #(.select(3), .width(32), .enable("false")) multiplexer_3 (
    .in0(Data2), .in1(Data6), .in2(Data10), .in3(Data14), .in4(Data18), .in5(Data22), .in6(Data26),
    .in7(Data30), .out(multiplexer_3_out), .sel(Data_Address[6:4]));
  Multiplexer #(.select(3), .width(32), .enable("false")) multiplexer_4 (
    .in0(Data3), .in1(Data7), .in2(Data11), .in3(Data15), .in4(Data19), .in5(Data23), .in6(Data27),
    .in7(Data31), .out(multiplexer_4_out), .sel(Data_Address[6:4]));
  Multiplexer #(.select(3), .enable("false")) multiplexer_5 (
    .in0(Valid0), .in1(Valid1), .in2(Valid2), .in3(Valid3), .in4(Valid4), .in5(Valid5), .in6(Valid6),
    .in7(Valid7), .out(ValidOut), .sel(Data_Address[6:4]));
  Multiplexer #(.select(3), .width(13), .enable("false")) multiplexer_6 (
    .in0(Tag0), .in1(Tag1), .in2(Tag2), .in3(Tag3), .in4(Tag4), .in5(Tag5), .in6(Tag6), .in7(Tag7),
    .out(TagOut), .sel(Data_Address[6:4]));
  Multiplexer #(.select(2), .width(32), .enable("false")) multiplexer_7 (
    .in0(multiplexer_1_out), .in1(multiplexer_2_out), .in2(multiplexer_3_out), .in3(multiplexer_4_out),
    .out({out_14[7:0], out_14[15:8], out_14[23:16], out_14[31:24]}), .sel(Data_Address[3:2]));

  assign out_13 = Data_Address[19:4];

  // Other names for the same wires on the sheet: OffSet[1:0] = Data_Address[3:2]; Line[2:0] = Data_Address[6:4];
  //   RamAddress[15:0] = Data_Address[19:4]; Tag[12:0] = Data_Address[19:7]; Data_Out[31:0] = out_14; Enable = in_2;
  //   Mask[3:0] = out_15; R = Reset; R_W = RW; Read_Time[3:0] = in_4; RO0[31:0] = Ram_Out_0; RO1[31:0] = Ram_Out_1;
  //   RO2[31:0] = Ram_Out_1_2; RO3[31:0] = Ram_Out_1_3; WD[31:0] = Write_Data; Write = R_W_out;
  //   Write_Time[3:0] = in_6

  // Notes on the sheet:
  //   Input
endmodule

module Control_CD (
  input  CLK,
  input  RW,
  input  Enable,
  input  [3:0] Read_Time,
  input  [3:0] Write_Time,
  output Read,
  output Write,
  output Finish_Read,
  output Valid,
  output CS
);

  wire and_1_out, and_2_out, and_3_out, and_4_out, and_5_out, comparator_1_eq, comparator_2_eq, CSR, CSW,
       Finish_Write, or_1_out, or_2_out;
  wire [3:0] counter_1_q, counter_2_q;

  and and_1 (and_1_out, Enable, Write, Finish_Write);
  and and_2 (and_2_out, Read, Enable);
  and and_3 (and_3_out, Enable, ~Write, ~RW);  // AND_Gate
  and and_4 (and_4_out, ~Write, ~Read, RW, Enable);  // AND_Gate
  and and_5 (and_5_out, Enable, Write, ~Finish_Write);  // AND_Gate
  or or_1 (or_1_out, and_2_out, and_1_out, and_3_out);
  or or_2 (or_2_out, and_4_out, and_5_out);
  D_Flip_Flop d_ff_1 (.clk(CLK), .D(or_1_out), .Q(Read));  // open: Qn, preset, en, reset
  D_Flip_Flop d_ff_2 (.clk(CLK), .D(or_2_out), .Q(Write));  // open: Qn, preset, en, reset
  not not_1 (Valid, Write);
  or or_3 (CS, CSR, CSW);
  D_Flip_Flop d_ff_3 (.clk(CLK), .D(Write), .Q(CSR));  // open: Qn, preset, en, reset
  D_Flip_Flop d_ff_4 (.clk(CLK), .D(Read), .Q(CSW));  // open: Qn, preset, en, reset
  Counter #(.width(4), .max('hf)) counter_1 (
    .load(Write), .D(Write_Time), .count(CSR), .Q(counter_1_q), .clk(CLK));  // open: carry, clr
  Counter #(.width(4), .max('hf)) counter_2 (
    .load(Read), .D(Read_Time), .count(CSW), .Q(counter_2_q), .clk(CLK));  // open: carry, clr
  Comparator #(.width(4)) comparator_1 (.a(counter_1_q), .b(4'b0000), .eq(comparator_1_eq));  // open: gt, lt
  Comparator #(.width(4)) comparator_2 (.a(counter_2_q), .b(4'b0000), .eq(comparator_2_eq));  // open: gt, lt
  and and_6 (Finish_Write, comparator_1_eq, CSR);
  and and_7 (Finish_Read, comparator_2_eq, CSW);

  // Other names for the same wires on the sheet: R_W = RW

  // Notes on the sheet:
  //   Input
  //   Output
endmodule

module Write_to_RAM (
  input  [31:0] Write_Data,
  input  [1:0] OffSet,
  input  RW,
  output [31:0] RAM_Input_0,
  output [31:0] RAM_Input_1,
  output [31:0] RAM_Input_2,
  output [31:0] RAM_Input_3,
  output [3:0] Mask
);

  Demultiplexer #(.select(2), .enable("false")) demultiplexer_1 (
    .out0(Mask[0]), .out1(Mask[1]), .out2(Mask[2]), .out3(Mask[3]), .in(RW), .sel(OffSet));
  Demultiplexer #(.select(2), .width(32), .enable("false")) demultiplexer_2 (
    .out0(RAM_Input_0), .out1(RAM_Input_1), .out2(RAM_Input_2), .out3(RAM_Input_3),
    .in({Write_Data[7:0], Write_Data[15:8], Write_Data[23:16], Write_Data[31:24]}), .sel(OffSet));

  // Other names for the same wires on the sheet: WD[31:0] = Write_Data; R_W = RW

  // Notes on the sheet:
  //   Input
  //   Output
endmodule
